# Fritzing sketch 5V Regulator schematic (saved by Fritzing 0.9.2b)
breadboards: 1

parts:
  Power_plug_(5_1V-12V) = Power plug
  USB_female_plug = USB Connectors [package=usb-a-s-nosilk]
  TIP42 = PNP-Transistor [package="TO92 [THT]"]
  LM317 = Voltage Regulator - Variable [package="TO220 [THT]"]
  part = Resistor [tolerance=±2% resistance=620 package=THT]
  part_2 = smd LED [color="Red (633nm)" package="0603 [SMD]"]
  part_3 = smd LED [color="Red (633nm)" package="0603 [SMD]"]

nets:
  N1: Power_plug_(5_1V-12V).VCC, TIP42.E
  GND: Power_plug_(5_1V-12V).GND, USB_female_plug.GND, LM317.ADJ, part.Pin_1
  N2: USB_female_plug.D+, TIP42.C, part_3.anode
  N3: TIP42.B, LM317.IN
  N4: LM317.OUT, part.Pin_0, part_2.cathode
  N5: part_2.anode, part_3.cathode
