# Fritzing sketch Circuit schematic (saved by Fritzing 0.9.2b)
breadboards: 1

parts:
  part = Zener Diode [part_number=1N4732A breakdown_voltage=5.1V package="Melf DO-213 AB [SMD]"]
  X1 = USB Connectors [package=usb-a-s]
  Cell_1 = SOLAR-IXYS [package=solarbit-12x1]
  C1 = Electrolytic Capacitor [capacitance=10µF voltage=10V package="100 mil [THT, electrolytic]"]
  Cell_2 = SOLAR-IXYS [package=solarbit-12x1]
  Cell_3 = SOLAR-IXYS [package=solarbit-12x1]
  Cell_4 = SOLAR-IXYS [package=solarbit-12x1]
  Cell_5 = SOLAR-IXYS [package=solarbit-12x1]
  Cell_6 = SOLAR-IXYS [package=solarbit-12x1]

nets:
  GND: part.cathode, part.anode, X1.D+, X1.GND, Cell_1.A, Cell_1.C, C1.-, C1.+, Cell_2.A, Cell_2.C, Cell_3.A, Cell_3.C, Cell_4.A, Cell_4.C, Cell_5.A, Cell_5.C, Cell_6.A, Cell_6.C
